// Digital circuit DRAM.dig as structural Verilog
module DRAM (
  input  [3:0] Address_Bus,
  input  [1:0] Control_Bus,
  input  [3:0] Data_Bus,
  input  CLK,
  output [3:0] Data_Output
);

  wire and_1_out, and_2_out, and_3_out, and_4_out, and_5_out, and_6_out, and_7_out, and_8_out, and_9_out,
       and_10_out, and_11_out, and_12_out, and_13_out, and_14_out, and_15_out, and_16_out, decoder_1_out_0,
       decoder_1_out_1, decoder_1_out_2, decoder_1_out_3, decoder_1_out_4, decoder_1_out_5, decoder_1_out_6,
       decoder_1_out_7, decoder_1_out_8, decoder_1_out_9, decoder_1_out_10, decoder_1_out_11,
       decoder_1_out_12, decoder_1_out_13, decoder_1_out_14, decoder_1_out_15;
  wire [3:0] gpr_1_output, gpr_2_output, gpr_3_output, gpr_4_output, gpr_5_output, gpr_6_output,
       gpr_7_output, gpr_8_output, gpr_9_output, gpr_10_output, gpr_11_output, gpr_12_output, gpr_13_output,
       gpr_14_output, gpr_15_output, gpr_16_output;

  Decoder #(.Selector_Bits(4)) decoder_1 (
    .sel(Address_Bus), .out_0(decoder_1_out_0), .out_1(decoder_1_out_1), .out_2(decoder_1_out_2),
    .out_3(decoder_1_out_3), .out_4(decoder_1_out_4), .out_5(decoder_1_out_5), .out_6(decoder_1_out_6),
    .out_7(decoder_1_out_7), .out_8(decoder_1_out_8), .out_9(decoder_1_out_9), .out_10(decoder_1_out_10),
    .out_11(decoder_1_out_11), .out_12(decoder_1_out_12), .out_13(decoder_1_out_13),
    .out_14(decoder_1_out_14), .out_15(decoder_1_out_15));
  and and_1 (and_1_out, decoder_1_out_0, CLK);
  and and_2 (and_2_out, decoder_1_out_4, CLK);
  and and_3 (and_3_out, decoder_1_out_8, CLK);
  and and_4 (and_4_out, decoder_1_out_12, CLK);
  GPR gpr_1 (.Clear_Store_Load(Control_Bus), .Input(Data_Bus), .CLK(and_1_out), .Output(gpr_1_output));
  GPR gpr_2 (.Clear_Store_Load(Control_Bus), .Input(Data_Bus), .CLK(and_2_out), .Output(gpr_2_output));
  GPR gpr_3 (.Clear_Store_Load(Control_Bus), .Input(Data_Bus), .CLK(and_3_out), .Output(gpr_3_output));
  GPR gpr_4 (.Clear_Store_Load(Control_Bus), .Input(Data_Bus), .CLK(and_4_out), .Output(gpr_4_output));
  and and_5 (and_5_out, decoder_1_out_1, CLK);
  and and_6 (and_6_out, decoder_1_out_5, CLK);
  and and_7 (and_7_out, decoder_1_out_9, CLK);
  and and_8 (and_8_out, decoder_1_out_13, CLK);
  GPR gpr_5 (.Clear_Store_Load(Control_Bus), .Input(Data_Bus), .CLK(and_5_out), .Output(gpr_5_output));
  GPR gpr_6 (.Clear_Store_Load(Control_Bus), .Input(Data_Bus), .CLK(and_6_out), .Output(gpr_6_output));
  GPR gpr_7 (.Clear_Store_Load(Control_Bus), .Input(Data_Bus), .CLK(and_7_out), .Output(gpr_7_output));
  GPR gpr_8 (.Clear_Store_Load(Control_Bus), .Input(Data_Bus), .CLK(and_8_out), .Output(gpr_8_output));
  and and_9 (and_9_out, decoder_1_out_2, CLK);
  and and_10 (and_10_out, decoder_1_out_6, CLK);
  and and_11 (and_11_out, decoder_1_out_10, CLK);
  and and_12 (and_12_out, decoder_1_out_14, CLK);
  GPR gpr_9 (.Clear_Store_Load(Control_Bus), .Input(Data_Bus), .CLK(and_9_out), .Output(gpr_9_output));
  GPR gpr_10 (.Clear_Store_Load(Control_Bus), .Input(Data_Bus), .CLK(and_10_out), .Output(gpr_10_output));
  GPR gpr_11 (.Clear_Store_Load(Control_Bus), .Input(Data_Bus), .CLK(and_11_out), .Output(gpr_11_output));
  GPR gpr_12 (.Clear_Store_Load(Control_Bus), .Input(Data_Bus), .CLK(and_12_out), .Output(gpr_12_output));
  and and_13 (and_13_out, decoder_1_out_3, CLK);
  and and_14 (and_14_out, decoder_1_out_7, CLK);
  and and_15 (and_15_out, decoder_1_out_11, CLK);
  and and_16 (and_16_out, decoder_1_out_15, CLK);
  GPR gpr_13 (.Clear_Store_Load(Control_Bus), .Input(Data_Bus), .CLK(and_13_out), .Output(gpr_13_output));
  GPR gpr_14 (.Clear_Store_Load(Control_Bus), .Input(Data_Bus), .CLK(and_14_out), .Output(gpr_14_output));
  GPR gpr_15 (.Clear_Store_Load(Control_Bus), .Input(Data_Bus), .CLK(and_15_out), .Output(gpr_15_output));
  GPR gpr_16 (.Clear_Store_Load(Control_Bus), .Input(Data_Bus), .CLK(and_16_out), .Output(gpr_16_output));
  Multiplexer #(.Selector_Bits(4), .Bits(4)) multiplexer_1 (
    .sel(Address_Bus), .in_0(gpr_1_output), .in_1(gpr_5_output), .in_2(gpr_9_output), .in_3(gpr_13_output),
    .in_4(gpr_2_output), .in_5(gpr_6_output), .in_6(gpr_10_output), .in_7(gpr_14_output),
    .in_8(gpr_3_output), .in_9(gpr_7_output), .in_10(gpr_11_output), .in_11(gpr_15_output),
    .in_12(gpr_4_output), .in_13(gpr_8_output), .in_14(gpr_12_output), .in_15(gpr_16_output),
    .out(Data_Output));
endmodule
