// Digital circuit GPR.dig as structural Verilog
module GPR (
  input  [1:0] Clear_Store_Load,
  input  [3:0] Input,
  input  CLK,
  output [3:0] Output
);

  wire [3:0] multiplexer_1_out;

  Multiplexer #(.Selector_Bits(2), .Bits(4)) multiplexer_1 (
    .sel(Clear_Store_Load), .in_0(4'b0000), .in_1(Input), .in_2(Output), .in_3(4'b1111),
    .out(multiplexer_1_out));
  D_FF D_0 (.D(multiplexer_1_out[3]), .C(CLK), .Q(Output[3]));  // open: nQ
  D_FF D_1 (.D(multiplexer_1_out[2]), .C(CLK), .Q(Output[2]));  // open: nQ
  D_FF D_2 (.D(multiplexer_1_out[1]), .C(CLK), .Q(Output[1]));  // open: nQ
  D_FF D_3 (.D(multiplexer_1_out[0]), .C(CLK), .Q(Output[0]));  // open: nQ

  // Notes on the sheet:
  //   Clear_Store_Load: 0 = Clear 
  //   1= Store Input 
  //   2 = Load
  //   3. Set F (All bits 1)
endmodule
