// Digital circuit IR.dig as structural Verilog
module IR (
  input  [3:0] Data_In,
  input  Load,
  input  CLK,
  output [3:0] Instruction
);

  wire [3:0] multiplexer_1_out;

  Multiplexer #(.Bits(4)) multiplexer_1 (.sel(Load), .in_0(Instruction), .in_1(Data_In), .out(multiplexer_1_out));
  Register #(.Bits(4)) register_1 (.D(multiplexer_1_out), .C(CLK), .en(1'b1), .Q(Instruction));
endmodule
