// Digital circuit control_RType.dig as structural Verilog
module control_RType (
  input  CLK,
  output [4:0] States,
  output Increment_PC,
  output WriteBack,
  output IR_Hi_Write,
  output IR_LO_Write
);

  D_FF IF1 (.D(States[4]), .C(CLK), .Q(IR_Hi_Write));  // open: nQ
  D_FF IF2 (.D(IR_Hi_Write), .C(CLK), .Q(IR_LO_Write));  // open: nQ
  D_FF Decode (.D(IR_LO_Write), .C(CLK), .Q(States[2]));  // open: nQ
  D_FF Execute (.D(States[2]), .C(CLK), .Q(States[3]));  // open: nQ
  D_FF u_WriteBack (.D(States[3]), .C(CLK), .Q(States[4]));  // open: nQ
  or or_1 (Increment_PC, IR_Hi_Write, States[4]);

  assign States[1:0] = {IR_LO_Write, IR_Hi_Write};
  assign WriteBack = States[4];
endmodule
